// Logisim project circuito_painel_seven_segmentos_final_version.circ as structural Verilog: 1 circuit, main circuit main
module main (
  input  in_1,
  input  in_2,
  input  in_3,
  input  in_4
);

  wire and_1_out, and_2_out, and_3_out, and_4_out, and_5_out, and_6_out, and_7_out, and_8_out, and_9_out,
       and_10_out, and_11_out, and_12_out, and_13_out, and_14_out, and_15_out, and_16_out, and_17_out,
       and_18_out, and_19_out, and_20_out, and_21_out, and_22_out, and_23_out, and_24_out, and_25_out,
       and_26_out, and_27_out, and_28_out, and_29_out, and_30_out, and_31_out, and_32_out, and_33_out,
       and_34_out, and_35_out, and_36_out, and_37_out, and_38_out, and_39_out, and_40_out, and_41_out,
       and_42_out, and_43_out, and_44_out, nand_1_out, nor_1_out, nor_2_out, nor_3_out, nor_4_out, nor_5_out,
       nor_6_out, nor_7_out, nor_8_out, nor_9_out, nor_10_out, nor_11_out, nor_12_out, nor_13_out,
       nor_14_out, not_1_out, not_2_out, not_3_out, not_4_out, not_5_out, not_6_out, not_7_out, not_8_out,
       not_9_out, not_10_out, not_11_out, not_12_out, not_13_out, not_14_out, not_15_out, not_16_out,
       not_17_out, not_18_out, or_1_out, or_2_out, or_3_out, or_4_out, or_5_out, or_6_out, or_7_out, or_8_out;

  not not_1 (not_1_out, in_1);
  not not_2 (not_2_out, in_2);
  not not_3 (not_3_out, in_3);
  not not_4 (not_4_out, in_2);
  not not_5 (not_5_out, in_4);
  not not_6 (not_6_out, in_2);
  not not_7 (not_7_out, in_4);
  not not_8 (not_8_out, in_3);
  not not_9 (not_9_out, in_1);
  not not_10 (not_10_out, in_4);
  not not_11 (not_11_out, in_2);
  not not_12 (not_12_out, in_4);
  not not_13 (not_13_out, in_3);
  not not_14 (not_14_out, in_3);
  not not_15 (not_15_out, in_1);
  not not_16 (not_16_out, in_4);
  nor nor_1 (nor_1_out, in_4, in_3, in_2, in_1);
  or or_1 (or_1_out, in_4, in_3);
  nor nor_2 (nor_2_out, in_2, in_1);
  nor nor_3 (nor_3_out, in_4, in_3);
  and and_1 (and_1_out, in_2, not_1_out);
  and and_2 (and_2_out, in_4, in_3, in_2);
  not not_17 (not_17_out, in_1);
  nor nor_4 (nor_4_out, in_4, in_3);
  and and_3 (and_3_out, not_2_out, in_1);
  and and_4 (and_4_out, in_4, not_3_out);
  and and_5 (and_5_out, not_4_out, in_1);
  and and_6 (and_6_out, not_5_out, in_3);
  and and_7 (and_7_out, not_6_out, in_1);
  and and_8 (and_8_out, in_4, in_2, in_1);
  not not_18 (not_18_out, in_3);
  and and_9 (and_9_out, not_7_out, in_3);
  nand nand_1 (nand_1_out, in_2, in_1);
  and and_10 (and_10_out, in_4, in_3);
  nor nor_5 (nor_5_out, in_2, in_1);
  and and_11 (and_11_out, in_4, not_8_out);
  and and_12 (and_12_out, in_2, not_9_out);
  nor nor_6 (nor_6_out, in_4, in_3);
  and and_13 (and_13_out, in_2, in_1);
  and and_14 (and_14_out, not_10_out, in_3, in_2, in_1);
  and and_15 (and_15_out, in_4, in_3, in_2, in_1);
  and and_16 (and_16_out, in_3, in_2);
  nor nor_7 (nor_7_out, in_4, in_1);
  and and_17 (and_17_out, in_4, in_3, not_11_out, in_1);
  and and_18 (and_18_out, not_12_out, in_3);
  nor nor_8 (nor_8_out, in_2, in_1);
  nor nor_9 (nor_9_out, in_4, in_3, in_2, in_1);
  nor nor_10 (nor_10_out, in_4, in_3, in_2);
  and and_19 (and_19_out, in_3, in_1);
  nor nor_11 (nor_11_out, in_4, in_2);
  and and_20 (and_20_out, in_4, not_13_out, in_2, in_1);
  and and_21 (and_21_out, in_4, in_3);
  nor nor_12 (nor_12_out, in_2, in_1);
  and and_22 (and_22_out, in_4, not_14_out);
  nor nor_13 (nor_13_out, in_2, in_1);
  nor nor_14 (nor_14_out, in_4, in_3);
  and and_23 (and_23_out, in_2, not_15_out);
  and and_24 (and_24_out, in_4, not_16_out);
  and and_25 (and_25_out, in_3, in_2, in_1);
  and and_26 (and_26_out, or_1_out, nor_2_out);
  and and_27 (and_27_out, nor_3_out, and_1_out);
  and and_28 (and_28_out, and_2_out, not_17_out);
  and and_29 (and_29_out, nor_4_out, and_3_out);
  and and_30 (and_30_out, and_4_out, and_5_out);
  and and_31 (and_31_out, and_6_out, and_7_out);
  and and_32 (and_32_out, and_8_out, not_18_out);
  and and_33 (and_33_out, and_9_out, nand_1_out);
  and and_34 (and_34_out, and_10_out, nor_5_out);
  and and_35 (and_35_out, and_11_out, and_12_out);
  and and_36 (and_36_out, nor_6_out, and_13_out);
  and and_37 (and_37_out, and_16_out, nor_7_out);
  and and_38 (and_38_out, and_18_out, nor_8_out);
  and and_39 (and_39_out, nor_10_out, in_1);
  and and_40 (and_40_out, and_19_out, nor_11_out);
  and and_41 (and_41_out, and_21_out, nor_12_out);
  and and_42 (and_42_out, and_22_out, nor_13_out);
  and and_43 (and_43_out, nor_14_out, and_23_out);
  and and_44 (and_44_out, and_24_out, and_25_out);
  or or_2 (or_2_out, nor_1_out, and_33_out, and_34_out, and_35_out, and_28_out, and_29_out, and_30_out, and_36_out, and_14_out, and_15_out);
  or or_3 (or_3_out, nor_1_out, and_27_out, and_35_out, and_37_out, and_29_out, and_30_out, and_31_out, and_17_out, and_36_out, and_14_out, and_15_out);
  or or_4 (or_4_out, and_38_out, and_34_out, and_27_out, and_35_out, and_37_out, and_29_out, and_30_out, and_31_out, and_17_out, and_32_out, and_14_out, and_15_out);
  or or_5 (or_5_out, nor_9_out, and_38_out, and_37_out, and_39_out, and_40_out, and_17_out, and_36_out, and_20_out, and_14_out, and_15_out);
  or or_6 (or_6_out, nor_9_out, and_38_out, and_41_out, and_35_out, and_37_out, and_14_out, and_39_out, and_30_out, and_17_out, and_36_out, and_20_out);
  or or_7 (or_7_out, nor_9_out, and_42_out, and_41_out, and_43_out, and_35_out, and_37_out, and_28_out, and_39_out, and_30_out, and_40_out, and_17_out, and_20_out);
  or or_8 (or_8_out, nor_1_out, and_26_out, and_27_out, and_28_out, and_29_out, and_30_out, and_31_out, and_32_out);
  _7_Segment_Display u_7_segment_display_1 (
    .g(or_4_out), .f(or_3_out), .a(or_2_out), .b(or_8_out), .e(or_5_out), .d(or_6_out), .c(or_7_out),
    .dp(and_44_out));

  // Notes on the sheet:
  //   Condição do 0
  //   Condição do 3
  //   Condição do 5
  //   Condição do C(12)
  //   Condição do E(14)
  //   Condição do F(15)
  //   Condição do 6
  //   Condiçao do 1
  //   Condiçao do 4
  //   Condição do 1,2,3
  //   Condição do 4
  //   Condição do 7
  //   Condição do 8
  //   Condição do 9
  //   Condição do A(10)
  //   Condição do D(13)
  //   Condição do 2, 6,A(10)
  //   Condição do B(11)
  //   Condição do 2
  //   Condição do 0
  //   Condição do 8
  //   Condição do A(10)
  //   Condição do D(13)
  //   Condiçao do 3
  //   CONDIÇAO DO PONTO
  //   CONDIÇÕES DO TRAÇO SUPERIOR DIREITO
  //   CONDIÇÕES DO TRAÇO SUPERIOR
  //   CONDIÇÕES DO TRAÇO DO MEIO
  //   CONDIÇOES DO TRAÇO INFERIOR
  //   CONDIÇOES DO TRAÇO INFERIOR DIREITO
  //   CONDIÇÕES DO TRAÇO SUPERIOR ESQUERDO
  //   CONDIÇÕES DO TRAÇO INFERIOR ESQUERDO
endmodule
